// Logisim project CargaParalela.circ as structural Verilog: 1 circuit, main circuit main
module main (
  input  clock,
  input  [3:0] entrada,
  input  in_3,
  output [3:0] saida
);

  D_Flip_Flop #(.trigger("falling")) d_ff_1 (
    .clk(clock), .D(entrada[0]), .Q(saida[0]), .reset(in_3));  // open: Qn, preset
  D_Flip_Flop #(.trigger("falling")) d_ff_2 (
    .clk(clock), .D(entrada[1]), .Q(saida[1]), .reset(in_3));  // open: Qn, preset
  D_Flip_Flop #(.trigger("falling")) d_ff_3 (
    .clk(clock), .D(entrada[2]), .Q(saida[2]), .reset(in_3));  // open: Qn, preset
  D_Flip_Flop #(.trigger("falling")) d_ff_4 (
    .clk(clock), .D(entrada[3]), .Q(saida[3]), .reset(in_3));  // open: Qn, preset
endmodule
