// Logisim project Controlador.circ as structural Verilog: 1 circuit, main circuit main
module main (
  input  [15:0] Entrada,
  output [3:0] OPERANDO,
  output [3:0] Operando_JUMP,
  output ResetPC,
  output [1:0] ULA,
  output ReiniciaReg,
  output [1:0] RgIN,
  output Reg1,
  output JUMP,
  output Reg2
);

  wire not_1_out, not_2_out, not_3_out, not_4_out;

  Demultiplexer #(.select(2), .width(4), .enable("false")) demultiplexer_1 (
    .out0(OPERANDO), .out3(Operando_JUMP), .in(Entrada[3:0]), .sel(Entrada[11:10]));  // open: out1, out2
  not not_1 (not_1_out, Entrada[15]);
  not not_2 (not_2_out, Entrada[14]);
  and and_1 (Reg1, Entrada[14], not_1_out);
  and and_2 (Reg2, not_2_out, Entrada[15]);
  not not_3 (not_3_out, Entrada[10]);
  and and_3 (ResetPC, not_3_out, Entrada[11]);
  and and_4 (ReiniciaReg, Entrada[10], not_4_out);
  not not_4 (not_4_out, Entrada[11]);
  and and_5 (JUMP, Entrada[11], Entrada[10]);

  assign RgIN = Entrada[13:12];
  assign ULA = Entrada[9:8];
endmodule
