// Logisim project Escolhe_Jump.circ as structural Verilog: 1 circuit, main circuit main
module main (
  input  [1:0] JMP_IN,
  output ULA,
  output REG,
  output CONT,
  output JUMP
);

  wire not_1_out, not_2_out, not_3_out, not_4_out;

  not not_1 (not_1_out, JMP_IN[0]);
  not not_2 (not_2_out, JMP_IN[1]);
  and and_1 (ULA, not_2_out, not_1_out);
  not not_3 (not_3_out, JMP_IN[1]);
  and and_2 (REG, not_3_out, JMP_IN[0]);
  not not_4 (not_4_out, JMP_IN[0]);
  and and_3 (CONT, JMP_IN[1], not_4_out);
  and and_4 (JUMP, JMP_IN[1], JMP_IN[0]);

  // Other names for the same wires on the sheet: JMP_OP[1:0] = JMP_IN
endmodule
