// Logisim project Proj1.circ as structural Verilog: 1 circuit, main circuit main
module main (
);

  wire ajuste_clearcont_1_out, and_1_out, and_2_out, and_3_out, and_4_out, and_5_out, CReg, d_ff_1_q,
       digital_oscilloscope_1_p10, JUMP, K0, K1, K2, K3, L0, L1, L2, L3, L4, L5, L6, L7, L8, L9, not_1_out,
       not_2_out, not_3_out, Reg1, Reg2, resetPC, ResetReg, S0, S1, S2, S3, S4, S5, S6, S7, S8, S9;
  wire [1:0] main_2_rgin, ULA;
  wire [3:0] HEX0, HEX1, HEX2, HEX3, HEX4, HEX5, Operando, OpJUMP, register_1_q, ResultIN, ResultULA;

  Hex_Digit_Display hex_digit_display_1 (.value(HEX5));  // open: dp
  LED u_L9 (.in(L9));
  // DipSwitch #(.NSwitches(1)) S8: pin names not known; wires that end beside it: S8
  // DipSwitch #(.NSwitches(1)) S9: pin names not known; wires that end beside it: S9
  Hex_Digit_Display hex_digit_display_2 (.value(HEX4));  // open: dp
  LED u_L6 (.in(L6));
  LED u_L8 (.in(L8));
  LED u_L7 (.in(L7));
  // DipSwitch #(.NSwitches(1)) S6: pin names not known; wires that end beside it: S6
  // DipSwitch #(.NSwitches(1)) S7: pin names not known; wires that end beside it: S7
  Button u_K1 (.out(K1));
  Button u_K3 (.out(K3));
  Button u_K2 (.out(K2));
  Hex_Digit_Display hex_digit_display_3 (.value(HEX2));  // open: dp
  Hex_Digit_Display hex_digit_display_4 (.value(HEX3));  // open: dp
  LED u_L4 (.in(L4));
  LED u_L5 (.in(L5));
  LED u_L3 (.in(L3));
  // DipSwitch #(.NSwitches(1)) S3: pin names not known; wires that end beside it: S3
  // DipSwitch #(.NSwitches(1)) S4: pin names not known; wires that end beside it: S4
  // DipSwitch #(.NSwitches(1)) S5: pin names not known; wires that end beside it: S5
  Button u_K0 (.out(K0));
  Hex_Digit_Display hex_digit_display_5 (.value(HEX1));  // open: dp
  Hex_Digit_Display hex_digit_display_6 (.value(HEX0));  // open: dp
  LED u_L1 (.in(L1));
  LED u_L2 (.in(L2));
  // DipSwitch #(.NSwitches(1)) S1: pin names not known; wires that end beside it: S1
  // DipSwitch #(.NSwitches(1)) S2: pin names not known; wires that end beside it: S2
  // DipSwitch #(.NSwitches(1)) S0: pin names not known; wires that end beside it: S0, S0
  LED u_L0 (.in(L0));
  Register #(.width(4), .Select("low")) register_1 (.D(OpJUMP), .Q(register_1_q), .clk(S9));  // open: en, clr
  and and_1 (and_1_out, JUMP, S9);
  and and_2 (and_2_out, d_ff_1_q, S9);
  D_Flip_Flop #(.trigger("falling")) d_ff_1 (
    .clk(S9), .D(and_1_out), .Q(d_ff_1_q), .reset(not_1_out));  // open: Qn, preset
  not not_1 (not_1_out, S0);
  Contadorfechado_main main_1 (
    .CLK(S9), .OUT({L7, L6, L5, L4, L3, L2, L1, L0}), .jump(and_2_out), .\end (register_1_q),
    .CLEAR(ajuste_clearcont_1_out));
  Ajuste_ClearCont ajuste_clearcont_1 (
    .Out(ajuste_clearcont_1_out), .S0_in(S0), .ResetPC_in(resetPC), .ResetPc_in_2(resetPC), .S9_in(S9));
  not not_2 (not_2_out, S0);
  ROM #(.dataWidth(16), .Select("low")) rom_1 (
    .addr({L7, L6, L5, L4, L3, L2, L1, L0}), .data({HEX5, HEX4, HEX3, HEX2}));
  or or_1 (CReg, not_2_out, and_3_out);
  and and_3 (and_3_out, not_3_out, ResetReg);
  not not_3 (not_3_out, S9);
  Controlador_main main_2 (
    .Entrada({HEX5, HEX4, HEX3, HEX2}), .OPERANDO(Operando), .ULA(ULA), .RgIN(main_2_rgin), .Reg1(Reg1),
    .Reg2(Reg2), .Operando_JUMP(OpJUMP), .ReiniciaReg(ResetReg), .ResetPC(resetPC), .JUMP(JUMP));
  CargaParalela_main main_3 (.saida(HEX1), .clock(and_4_out), .entrada(ResultULA), .in_3(CReg));
  and and_4 (and_4_out, S9, Reg1);
  Multiplexer #(.select(2), .width(4), .enable("false")) multiplexer_1 (
    .in1(HEX1), .in2(HEX0), .out(ResultIN), .sel(main_2_rgin));  // open: in0, in3
  ULA_Completa_main main_4 (.RgIN(ResultIN), .Operando(Operando), .Result(ResultULA), .ULA(ULA));
  and and_5 (and_5_out, S9, Reg2);
  CargaParalela_main main_5 (.saida(HEX0), .clock(and_5_out), .entrada(ResultULA), .in_3(CReg));
  // Digital_Oscilloscope digital_oscilloscope_1: pin names not known; wires that end beside it: S9, L0, L1, L2, L3, L4, L5, L6, L7, digital_oscilloscope_1_p10
  Button button_1 (.out(digital_oscilloscope_1_p10));

  // Other names for the same wires on the sheet: SReg1[3:0] = HEX1; SReg2[3:0] = HEX0

  // Notes on the sheet:
  //   contents of rom_1 (hex, n*v repeats v):
  //   6005 9101 6202 6304 c08 0 0 0 400 6001 9001 9002 6302 6102 9302 6200 6001 800 6003 800
endmodule
