// Logisim project Util.circ as structural Verilog
module Ajuste_ClearCont (
  input  S0_in,
  input  ResetPC_in,
  input  ResetPc_in_2,
  input  S9_in,
  output Out
);

  wire and_1_out, and_2_out, not_1_out, not_2_out, not_4_out, or_1_out;

  and and_1 (and_1_out, not_1_out, not_2_out);
  not not_1 (not_1_out, S0_in);
  not not_2 (not_2_out, ResetPC_in);
  not not_3 (Out, or_1_out);
  or or_1 (or_1_out, and_1_out, and_2_out);
  and and_2 (and_2_out, ResetPc_in_2, not_4_out);
  not not_4 (not_4_out, S9_in);
endmodule

// JMP_Ajuste
module Ajuste_Jump (
  input  CLK_in,
  input  CLK_in_2,
  input  M_Clear_in,
  input  Jump_in,
  input  CLK_in_3,
  output out
);

  wire and_1_out, d_ff_1_q, not_1_out;

  and and_1 (and_1_out, Jump_in, CLK_in_3);
  D_Flip_Flop #(.trigger("falling")) d_ff_1 (
    .clk(CLK_in_2), .D(and_1_out), .Q(d_ff_1_q), .reset(not_1_out));  // open: Qn, preset
  not not_1 (not_1_out, M_Clear_in);
  and and_2 (out, d_ff_1_q, CLK_in);
endmodule
