// Logisim project Proj1.circ as structural Verilog: 1 circuit, main circuit main
module main (
  output [15:0] out_1
);

  wire digital_oscilloscope_1_p10, K0, K1, K2, K3, L0, L1, L2, L3, L4, L5, L6, L7, L8, L9, S0, S1, S2, S3,
       S4, S5, S6, S7, S8, S9;
  wire [3:0] HEX0, HEX1;

  Hex_Digit_Display hex_digit_display_1 (.value(out_1[15:12]));  // open: dp
  LED u_L9 (.in(L9));
  // DipSwitch #(.NSwitches(1)) S9: pin names not known; wires that end beside it: S9
  // DipSwitch #(.NSwitches(1)) S8: pin names not known; wires that end beside it: S8
  Hex_Digit_Display hex_digit_display_2 (.value(out_1[11:8]));  // open: dp
  LED u_L8 (.in(L8));
  LED u_L7 (.in(L7));
  LED u_L6 (.in(L6));
  // DipSwitch #(.NSwitches(1)) S7: pin names not known; wires that end beside it: S7
  // DipSwitch #(.NSwitches(1)) S6: pin names not known; wires that end beside it: S6
  Hex_Digit_Display hex_digit_display_3 (.value(out_1[7:4]));  // open: dp
  Hex_Digit_Display hex_digit_display_4 (.value(out_1[3:0]));  // open: dp
  LED u_L3 (.in(L3));
  LED u_L4 (.in(L4));
  LED u_L5 (.in(L5));
  // DipSwitch #(.NSwitches(1)) S3: pin names not known; wires that end beside it: S3
  // DipSwitch #(.NSwitches(1)) S4: pin names not known; wires that end beside it: S4
  // DipSwitch #(.NSwitches(1)) S5: pin names not known; wires that end beside it: S5
  Hex_Digit_Display hex_digit_display_5 (.value(HEX0));  // open: dp
  Hex_Digit_Display hex_digit_display_6 (.value(HEX1));  // open: dp
  LED u_L1 (.in(L1));
  LED u_L2 (.in(L2));
  // DipSwitch #(.NSwitches(1)) S2: pin names not known; wires that end beside it: S2
  // DipSwitch #(.NSwitches(1)) S1: pin names not known; wires that end beside it: S1
  // DipSwitch #(.NSwitches(1)) S0: pin names not known; wires that end beside it: S0
  LED u_L0 (.in(L0));
  Button u_K2 (.out(K2));
  Button u_K3 (.out(K3));
  Button u_K1 (.out(K1));
  Button u_K0 (.out(K0));
  Contadorfechado_main main_1 (.in_1(S9), .out_3({L7, L6, L5, L4, L3, L2, L1, L0}), .in_2(S0));
  ROM #(.dataWidth(16), .Select("low")) rom_1 (.addr({L7, L6, L5, L4, L3, L2, L1, L0}), .data(out_1));
  // Digital_Oscilloscope digital_oscilloscope_1: pin names not known; wires that end beside it: S9, L0, L1, L2, L3, L4, L5, L6, L7, digital_oscilloscope_1_p10
  Button button_1 (.out(digital_oscilloscope_1_p10));

  // Other names for the same wires on the sheet: HEX2[3:0] = out_1[3:0]; HEX3[3:0] = out_1[7:4];
  //   HEX4[3:0] = out_1[11:8]; HEX5[3:0] = out_1[15:12]

  // Notes on the sheet:
  //   contents of rom_1 (hex, n*v repeats v):
  //   6004 9102 6201 6305 9002 6002 9003 400 c0d 4*0 9002 6302 6101 9302 6200 6003 800
endmodule
