// Logisim project Contadorfechado.circ as structural Verilog: 2 circuits, main circuit main
module main (
  input  CLK,
  input  CLEAR,
  input  jump,
  input  [3:0] \end ,
  output [7:0] OUT
);

  wire and_1_out, and_2_out, and_3_out, and_4_out, and_5_out, and_6_out, r0, r1, r2, r3, s0, s1, s2, s3;

  circuito_jump_main main_1 (.ENDERECO(\end [0]), .JUMP(jump), .CLEAR(CLEAR), .VAI_NO_SET(s0), .VAI_NO_RESET(r0));
  T_Flip_Flop #(.NegatePresetClear("true")) t_ff_1 (
    .clk(CLK), .T(1'b1), .Q(OUT[0]), .preset(s0), .reset(r0));  // open: Qn
  T_Flip_Flop #(.NegatePresetClear("true")) t_ff_2 (
    .clk(CLK), .T(OUT[0]), .Q(OUT[1]), .preset(s1), .reset(r1));  // open: Qn
  circuito_jump_main main_2 (.ENDERECO(\end [1]), .JUMP(jump), .CLEAR(CLEAR), .VAI_NO_SET(s1), .VAI_NO_RESET(r1));
  and and_1 (and_1_out, OUT[1], OUT[0]);
  T_Flip_Flop #(.NegatePresetClear("true")) t_ff_3 (
    .clk(CLK), .T(and_1_out), .Q(OUT[2]), .preset(s2), .reset(r2));  // open: Qn
  circuito_jump_main main_3 (.ENDERECO(\end [2]), .JUMP(jump), .CLEAR(CLEAR), .VAI_NO_SET(s2), .VAI_NO_RESET(r2));
  and and_2 (and_2_out, OUT[2], and_1_out);
  T_Flip_Flop #(.NegatePresetClear("true")) t_ff_4 (
    .clk(CLK), .T(and_2_out), .Q(OUT[3]), .preset(s3), .reset(r3));  // open: Qn
  and and_3 (and_3_out, OUT[3], and_2_out);
  circuito_jump_main main_4 (.ENDERECO(\end [3]), .JUMP(jump), .CLEAR(CLEAR), .VAI_NO_SET(s3), .VAI_NO_RESET(r3));
  T_Flip_Flop #(.NegatePresetClear("true")) t_ff_5 (
    .clk(CLK), .T(and_3_out), .Q(OUT[4]), .reset(CLEAR));  // open: Qn, preset
  and and_4 (and_4_out, OUT[4], and_3_out);
  T_Flip_Flop #(.NegatePresetClear("true")) t_ff_6 (
    .clk(CLK), .T(and_4_out), .Q(OUT[5]), .reset(CLEAR));  // open: Qn, preset
  and and_5 (and_5_out, OUT[5], and_4_out);
  T_Flip_Flop #(.NegatePresetClear("true")) t_ff_7 (
    .clk(CLK), .T(and_5_out), .Q(OUT[6]), .reset(CLEAR));  // open: Qn, preset
  and and_6 (and_6_out, OUT[6], and_5_out);
  T_Flip_Flop #(.NegatePresetClear("true")) t_ff_8 (
    .clk(CLK), .T(and_6_out), .Q(OUT[7]), .reset(CLEAR));  // open: Qn, preset

  // Other names for the same wires on the sheet: JMP = jump

  // Notes on the sheet:
  //   Q1
endmodule

module l (
);

  main main_1 ();  // open: CLK, OUT, jump, end, CLEAR
endmodule
