// Logisim project RegistradorFechado.circ as structural Verilog: 2 circuits, main circuit Reg1
module Reg1 (
  input  [3:0] D,
  input  CLK,
  input  LOAD,
  output [3:0] Q
);

  Registrador_main main_1 (
    .CLK(CLK), .LOAD(LOAD), .D0(D[0]), .D1(D[1]), .D2(D[2]), .D3(D[3]), .Q0(Q[0]), .Q1(Q[1]), .Q2(Q[2]),
    .Q3(Q[3]));
endmodule

// clk
module Reg2 (
  input  [3:0] in_1,
  input  CLK,
  input  LOAD,
  output [3:0] out_4
);

  Registrador_main main_1 (
    .CLK(CLK), .LOAD(LOAD), .D0(in_1[0]), .D1(in_1[1]), .D2(in_1[2]), .D3(in_1[3]), .Q0(out_4[0]),
    .Q1(out_4[1]), .Q2(out_4[2]), .Q3(out_4[3]));
endmodule
