// Logisim project Contadorfechado.circ as structural Verilog: 2 circuits, main circuit main
module main (
  input  CLK,
  input  jump,
  input  CLEAR,
  input  [3:0] \end ,
  output [7:0] OUT
);

  wire and_1_out, and_2_out, and_3_out, and_4_out, and_5_out, and_6_out, r0, r1, r2, r3, r4, r5, r6, r7, s0,
       s1, s2, s3, s4, s5, s6, s7;

  T_Flip_Flop #(.NegatePresetClear("true")) t_ff_1 (
    .clk(CLK), .T(1'b1), .Q(OUT[0]), .preset(s0), .reset(r0));  // open: Qn
  T_Flip_Flop #(.NegatePresetClear("true")) t_ff_2 (
    .clk(CLK), .T(OUT[0]), .Q(OUT[1]), .preset(s1), .reset(r1));  // open: Qn
  and and_1 (and_1_out, OUT[1], OUT[0]);
  T_Flip_Flop #(.NegatePresetClear("true")) t_ff_3 (
    .clk(CLK), .T(and_1_out), .Q(OUT[2]), .preset(s2), .reset(r2));  // open: Qn
  jump_fechado jump_fechado_1 (
    .end0(\end [0]), .jump0(jump), .clear0(CLEAR), .end1(\end [1]), .jump1(jump), .clear1(CLEAR),
    .end2(\end [2]), .jump2(jump), .clear2(CLEAR), .end3(\end [3]), .jump3(jump), .clear3(CLEAR),
    .end4(1'b0), .jump4(jump), .clear4(CLEAR), .end5(1'b0), .jump5(jump), .clear5(CLEAR), .end6(1'b0),
    .jump6(jump), .clear6(CLEAR), .end7(1'b0), .jump7(jump), .clear7(CLEAR), .set0(s0), .reset0(r0),
    .set1(s1), .reset1(r1), .set2(s2), .reset2(r2), .set3(s3), .reset3(r3), .set4(s4), .reset4(r4),
    .set5(s5), .reset5(r5), .set6(s6), .reset6(r6), .set7(s7), .reset7(r7));
  and and_2 (and_2_out, OUT[2], and_1_out);
  T_Flip_Flop #(.NegatePresetClear("true")) t_ff_4 (
    .clk(CLK), .T(and_2_out), .Q(OUT[3]), .preset(s3), .reset(r3));  // open: Qn
  and and_3 (and_3_out, OUT[3], and_2_out);
  T_Flip_Flop #(.NegatePresetClear("true")) t_ff_5 (
    .clk(CLK), .T(and_3_out), .Q(OUT[4]), .preset(s4), .reset(r4));  // open: Qn
  and and_4 (and_4_out, OUT[4], and_3_out);
  T_Flip_Flop #(.NegatePresetClear("true")) t_ff_6 (
    .clk(CLK), .T(and_4_out), .Q(OUT[5]), .preset(s5), .reset(r5));  // open: Qn
  and and_5 (and_5_out, OUT[5], and_4_out);
  T_Flip_Flop #(.NegatePresetClear("true")) t_ff_7 (
    .clk(CLK), .T(and_5_out), .Q(OUT[6]), .preset(s6), .reset(r6));  // open: Qn
  and and_6 (and_6_out, OUT[6], and_5_out);
  T_Flip_Flop #(.NegatePresetClear("true")) t_ff_8 (
    .clk(CLK), .T(and_6_out), .Q(OUT[7]), .preset(s7), .reset(r7));  // open: Qn

  // Notes on the sheet:
  //   Q1
endmodule

module l (
);

  main main_1 ();  // open: CLK, OUT, end, jump, CLEAR
endmodule
