// Logisim project Dica_JUMP.circ as structural Verilog: 4 circuits, main circuit main
module main (
  input  CLK,
  input  Master_Clear__0_para_ativar,
  output [7:0] CLK_2
);

  wire and_1_out, and_2_out, D00, D01, D02, D03, D04, D05, D06, D07, D08, D09, D10, D11, D12, D13, D14, D15,
       not_1_out, or_1_out;

  Hex_Digit_Display hex_digit_display_1 (.value({D15, D14, D13, D12}));  // open: dp
  Hex_Digit_Display hex_digit_display_2 (.value({D11, D10, D09, D08}));  // open: dp
  Hex_Digit_Display hex_digit_display_3 (.value({D03, D02, D01, D00}));  // open: dp
  Hex_Digit_Display hex_digit_display_4 (.value({D07, D06, D05, D04}));  // open: dp
  or or_1 (or_1_out, ~D11, D10);  // OR_Gate
  and and_1 (and_1_out, CLK, D11, D10);
  Contador contador_1 (
    .Clock__Borda_de_subida(CLK), .Qout__8_bits(CLK_2), .Jump(and_1_out),
    .A__Addr_para_Jump_4Bits({D03, D02, D01, D00}), .CLR(and_2_out));
  and and_2 (and_2_out, or_1_out, Master_Clear__0_para_ativar);
  not not_1 (not_1_out, CLK);
  ROM rom_1 (
    .Addr__8Bits(CLK_2), .Clock__Borda_de_subida(not_1_out),
    .Data_Out__16Bits({D15, D14, D13, D12, D11, D10, D09, D08, D07, D06, D05, D04, D03, D02, D01, D00}));
endmodule

module Contador (
  input  Clock__Borda_de_subida,
  input  Jump,
  input  CLR,
  input  [3:0] A__Addr_para_Jump_4Bits,
  output [7:0] Qout__8_bits
);

  wire and_6_out, and_8_out, and_9_out, and_10_out, nand_1_out, nand_2_out, nand_3_out, nand_4_out, or_1_out,
       or_2_out, or_3_out, or_4_out, T2, T3, T4, T5, T6, T7;

  and and_1 (T7, Qout__8_bits[6], T6);
  LED L6 (.in(Qout__8_bits[6]));
  LED L4 (.in(Qout__8_bits[4]));
  LED L5 (.in(Qout__8_bits[5]));
  LED L7 (.in(Qout__8_bits[7]));
  T_Flip_Flop #(.NegatePresetClear("true")) t_ff_1 (
    .clk(Clock__Borda_de_subida), .T(T7), .Q(Qout__8_bits[7]), .reset(CLR));  // open: Qn, preset
  and and_2 (T6, Qout__8_bits[5], T5);
  LED L3 (.in(Qout__8_bits[3]));
  LED L1 (.in(Qout__8_bits[1]));
  LED L2 (.in(Qout__8_bits[2]));
  LED L0 (.in(Qout__8_bits[0]));
  and and_3 (T5, Qout__8_bits[4], T4);
  T_Flip_Flop #(.NegatePresetClear("true")) t_ff_2 (
    .clk(Clock__Borda_de_subida), .T(T6), .Q(Qout__8_bits[6]), .reset(CLR));  // open: Qn, preset
  T_Flip_Flop #(.NegatePresetClear("true")) t_ff_3 (
    .clk(Clock__Borda_de_subida), .T(T5), .Q(Qout__8_bits[5]), .reset(CLR));  // open: Qn, preset
  and and_4 (T4, Qout__8_bits[3], T3);
  T_Flip_Flop #(.NegatePresetClear("true")) t_ff_4 (
    .clk(Clock__Borda_de_subida), .T(T4), .Q(Qout__8_bits[4]), .reset(CLR));  // open: Qn, preset
  and and_5 (T3, Qout__8_bits[2], T2);
  nand nand_1 (nand_1_out, Jump, A__Addr_para_Jump_4Bits[3]);
  T_Flip_Flop #(.NegatePresetClear("true")) t_ff_5 (
    .clk(Clock__Borda_de_subida), .T(T3), .Q(Qout__8_bits[3]), .preset(nand_1_out), .reset(and_6_out));  // open: Qn
  and and_6 (and_6_out, or_1_out, CLR);
  or or_1 (or_1_out, A__Addr_para_Jump_4Bits[3], ~Jump);  // OR_Gate
  and and_7 (T2, Qout__8_bits[1], Qout__8_bits[0]);
  nand nand_2 (nand_2_out, Jump, A__Addr_para_Jump_4Bits[2]);
  T_Flip_Flop #(.NegatePresetClear("true")) t_ff_6 (
    .clk(Clock__Borda_de_subida), .T(T2), .Q(Qout__8_bits[2]), .preset(nand_2_out), .reset(and_8_out));  // open: Qn
  and and_8 (and_8_out, or_2_out, CLR);
  or or_2 (or_2_out, A__Addr_para_Jump_4Bits[2], ~Jump);  // OR_Gate
  nand nand_3 (nand_3_out, Jump, A__Addr_para_Jump_4Bits[1]);
  T_Flip_Flop #(.NegatePresetClear("true")) t_ff_7 (
    .clk(Clock__Borda_de_subida), .T(Qout__8_bits[0]), .Q(Qout__8_bits[1]), .preset(nand_3_out),
    .reset(and_9_out));  // open: Qn
  and and_9 (and_9_out, or_3_out, CLR);
  or or_3 (or_3_out, A__Addr_para_Jump_4Bits[1], ~Jump);  // OR_Gate
  nand nand_4 (nand_4_out, Jump, A__Addr_para_Jump_4Bits[0]);
  and and_10 (and_10_out, or_4_out, CLR);
  or or_4 (or_4_out, A__Addr_para_Jump_4Bits[0], ~Jump);  // OR_Gate
  T_Flip_Flop #(.NegatePresetClear("true")) t_ff_8 (
    .clk(Clock__Borda_de_subida), .T(1'b1), .Q(Qout__8_bits[0]), .preset(nand_4_out), .reset(and_10_out));  // open: Qn

  // Other names for the same wires on the sheet: A0 = A__Addr_para_Jump_4Bits[0]; A1 = A__Addr_para_Jump_4Bits[1];
  //   A2 = A__Addr_para_Jump_4Bits[2]; A3 = A__Addr_para_Jump_4Bits[3]; CLK = Clock__Borda_de_subida; JMP = Jump;
  //   Q0 = Qout__8_bits[0]; Q1 = Qout__8_bits[1]; Q2 = Qout__8_bits[2]; Q3 = Qout__8_bits[3]; Q4 = Qout__8_bits[4];
  //   Q5 = Qout__8_bits[5]; Q6 = Qout__8_bits[6]; Q7 = Qout__8_bits[7]
endmodule

module Registrador (
  input  [3:0] Din__4_bits,
  input  Clock__Borda_de_subida,
  output [3:0] Qout__4_bits
);

  D_Flip_Flop d_ff_1 (
    .clk(Clock__Borda_de_subida), .D(Din__4_bits[3]), .Q(Qout__4_bits[3]));  // open: Qn, preset, reset
  D_Flip_Flop d_ff_2 (
    .clk(Clock__Borda_de_subida), .D(Din__4_bits[2]), .Q(Qout__4_bits[2]));  // open: Qn, preset, reset
  D_Flip_Flop d_ff_3 (
    .clk(Clock__Borda_de_subida), .D(Din__4_bits[1]), .Q(Qout__4_bits[1]));  // open: Qn, preset, reset
  D_Flip_Flop d_ff_4 (
    .clk(Clock__Borda_de_subida), .D(Din__4_bits[0]), .Q(Qout__4_bits[0]));  // open: Qn, preset, reset

  // Other names for the same wires on the sheet: CLK = Clock__Borda_de_subida; D0 = Din__4_bits[0];
  //   D1 = Din__4_bits[1]; D2 = Din__4_bits[2]; D3 = Din__4_bits[3]; Q0 = Qout__4_bits[0]; Q1 = Qout__4_bits[1];
  //   Q2 = Qout__4_bits[2]; Q3 = Qout__4_bits[3]
endmodule

module ROM (
  input  [7:0] Addr__8Bits,
  input  Clock__Borda_de_subida,
  output [15:0] Data_Out__16Bits
);

  wire [15:0] rom_1_data;

  ROM_part #(.dataWidth(16), .Select("low")) rom_1 (.addr(Addr__8Bits), .data(rom_1_data));
  Register #(.width(16), .Select("low")) register_1 (
    .D(rom_1_data), .Q(Data_Out__16Bits), .clk(Clock__Borda_de_subida));  // open: en, clr

  // Notes on the sheet:
  //   contents of rom_1 (hex, n*v repeats v):
  //   6005 9101 6202 6304 c08 0 0 0 400 6001 9001 9002 6302 6102 9302 6200 6001 800
endmodule
