// Logisim project Proj1.circ as structural Verilog: 1 circuit, main circuit main
module main (
);

  wire ajuste_clearcont_1_out, and_1_out, and_2_out, and_3_out, CReg, digital_oscilloscope_1_p10, JUMP, K0,
       K1, K2, K3, L0, L1, L2, L3, L4, L5, L6, L7, L8, L9, not_1_out, or_1_out, or_2_out, Reg1, Reg2,
       resetPC, ResetReg, S0, S1, S2, S3, S4, S5, S6, S7, S8, S9;
  wire [1:0] main_2_rgin, ULA;
  wire [3:0] HEX0, HEX1, HEX2, HEX3, HEX4, HEX5, Operando, OpJUMP, ResultIN, ResultULA;

  Hex_Digit_Display hex_digit_display_1 (.value(HEX5));  // open: dp
  LED u_L9 (.in(L9));
  // DipSwitch #(.NSwitches(1)) S8: pin names not known; wires that end beside it: S8
  // DipSwitch #(.NSwitches(1)) S9: pin names not known; wires that end beside it: S9
  Hex_Digit_Display hex_digit_display_2 (.value(HEX4));  // open: dp
  LED u_L6 (.in(L6));
  LED u_L7 (.in(L7));
  LED u_L8 (.in(L8));
  // DipSwitch #(.NSwitches(1)) S6: pin names not known; wires that end beside it: S6
  // DipSwitch #(.NSwitches(1)) S7: pin names not known; wires that end beside it: S7
  Button u_K2 (.out(K2));
  Button u_K3 (.out(K3));
  Button u_K1 (.out(K1));
  Hex_Digit_Display hex_digit_display_3 (.value(HEX3));  // open: dp
  Hex_Digit_Display hex_digit_display_4 (.value(HEX2));  // open: dp
  LED u_L3 (.in(L3));
  LED u_L5 (.in(L5));
  LED u_L4 (.in(L4));
  // DipSwitch #(.NSwitches(1)) S4: pin names not known; wires that end beside it: S4
  // DipSwitch #(.NSwitches(1)) S3: pin names not known; wires that end beside it: S3
  // DipSwitch #(.NSwitches(1)) S5: pin names not known; wires that end beside it: S5
  Button u_K0 (.out(K0));
  Hex_Digit_Display hex_digit_display_5 (.value(HEX1));  // open: dp
  Hex_Digit_Display hex_digit_display_6 (.value(HEX0));  // open: dp
  LED u_L2 (.in(L2));
  LED u_L1 (.in(L1));
  // DipSwitch #(.NSwitches(1)) S1: pin names not known; wires that end beside it: S1
  // DipSwitch #(.NSwitches(1)) S0: pin names not known; wires that end beside it: S0
  // DipSwitch #(.NSwitches(1)) S2: pin names not known; wires that end beside it: S2
  LED u_L0 (.in(L0));
  and and_1 (and_1_out, JUMP, not_1_out);
  not not_1 (not_1_out, S9);
  Contadorfechado_main main_1 (
    .CLK(S9), .OUT({L7, L6, L5, L4, L3, L2, L1, L0}), .\end (OpJUMP), .jump(and_1_out),
    .CLEAR(ajuste_clearcont_1_out));
  Ajuste_ClearCont ajuste_clearcont_1 (
    .Out(ajuste_clearcont_1_out), .S0_in(S0), .ResetPC_in(resetPC), .ResetPc_in_2(resetPC), .S9_in(S9));
  ROM #(.dataWidth(16), .Select("low")) rom_1 (
    .addr({L7, L6, L5, L4, L3, L2, L1, L0}), .data({HEX5, HEX4, HEX3, HEX2}));
  Ajuste_ClearReg ajuste_clearreg_1 (.Out(CReg), .S0_in(S0), .S9_in(S9), .ResetReg_in(ResetReg));
  Controlador_main main_2 (
    .Entrada({HEX5, HEX4, HEX3, HEX2}), .OPERANDO(Operando), .ULA(ULA), .RgIN(main_2_rgin), .Reg1(Reg1),
    .Reg2(Reg2), .Operando_JUMP(OpJUMP), .ReiniciaReg(ResetReg), .ResetPC(resetPC), .JUMP(JUMP));
  CargaParalela_main main_3 (.saida(HEX1), .clock(and_2_out), .entrada(ResultULA), .in_3(or_1_out));
  and and_2 (and_2_out, S9, Reg1);
  or or_1 (or_1_out, CReg, resetPC);
  Multiplexer #(.select(2), .width(4), .enable("false")) multiplexer_1 (
    .in1(HEX1), .in2(HEX0), .out(ResultIN), .sel(main_2_rgin));  // open: in0, in3
  ULA_Completa_main main_4 (.RgIN(ResultIN), .Operando(Operando), .Result(ResultULA), .ULA(ULA));
  and and_3 (and_3_out, S9, Reg2);
  CargaParalela_main main_5 (.saida(HEX0), .clock(and_3_out), .entrada(ResultULA), .in_3(or_2_out));
  or or_2 (or_2_out, CReg, resetPC);
  // Digital_Oscilloscope digital_oscilloscope_1: pin names not known; wires that end beside it: S9, L0, L1, L2, L3, L4, L5, L6, L7, digital_oscilloscope_1_p10
  Button button_1 (.out(digital_oscilloscope_1_p10));

  // Other names for the same wires on the sheet: Leds[7:0] = {L7, L6, L5, L4, L3, L2, L1, L0}; SReg1[3:0] = HEX1;
  //   SReg2[3:0] = HEX0

  // Notes on the sheet:
  //   contents of rom_1 (hex, n*v repeats v):
  //   6004 9102 6201 6305 9002 6002 9003 400 c0d 4*0 9002 6302 6101 9302 6200 6003 800
endmodule
