// Logisim project Registrador.circ as structural Verilog: 1 circuit, main circuit main
module main (
  input  D0,
  input  D1,
  input  D2,
  input  D3,
  input  CLK,
  input  LOAD,
  output Q0,
  output Q1,
  output Q2,
  output Q3
);

  wire multiplexer_1_out, multiplexer_2_out, multiplexer_3_out, multiplexer_4_out, not_1_out, not_2_out,
       not_3_out, not_4_out;

  Multiplexer #(.enable("false")) multiplexer_1 (.in0(Q0), .in1(D0), .out(multiplexer_1_out), .sel(LOAD));
  not not_1 (not_1_out, CLK);
  D_Flip_Flop d_ff_1 (.clk(not_1_out), .D(multiplexer_1_out), .Q(Q0));  // open: Qn, preset, reset
  Multiplexer #(.enable("false")) multiplexer_2 (.in0(Q1), .in1(D1), .out(multiplexer_2_out), .sel(LOAD));
  not not_2 (not_2_out, CLK);
  D_Flip_Flop d_ff_2 (.clk(not_2_out), .D(multiplexer_2_out), .Q(Q1));  // open: Qn, preset, reset
  Multiplexer #(.enable("false")) multiplexer_3 (.in0(Q2), .in1(D2), .out(multiplexer_3_out), .sel(LOAD));
  not not_3 (not_3_out, CLK);
  D_Flip_Flop d_ff_3 (.clk(not_3_out), .D(multiplexer_3_out), .Q(Q2));  // open: Qn, preset, reset
  Multiplexer #(.enable("false")) multiplexer_4 (.in0(Q3), .in1(D3), .out(multiplexer_4_out), .sel(LOAD));
  not not_4 (not_4_out, CLK);
  D_Flip_Flop d_ff_4 (.clk(not_4_out), .D(multiplexer_4_out), .Q(Q3));  // open: Qn, preset, reset
endmodule
