// Logisim project Util.circ as structural Verilog: 3 circuits, main circuit main
module main (
);

  // AND_Gate and_1 is placed but not wired
  // AND_Gate and_2 is placed but not wired
endmodule

module Ajuste_ClearCont (
  input  S0_in,
  input  ResetPC_in,
  input  ResetPc_in_2,
  input  S9_in,
  output Out
);

  wire and_1_out, and_2_out, not_1_out, not_2_out, not_4_out, or_1_out;

  and and_1 (and_1_out, not_2_out, not_1_out);
  not not_1 (not_1_out, ResetPC_in);
  not not_2 (not_2_out, S0_in);
  not not_3 (Out, or_1_out);
  or or_1 (or_1_out, and_1_out, and_2_out);
  and and_2 (and_2_out, ResetPc_in_2, not_4_out);
  not not_4 (not_4_out, S9_in);
endmodule

module Ajuste_ClearReg (
  input  S0_in,
  input  S9_in,
  input  ResetReg_in,
  output Out
);

  wire and_1_out, not_1_out, not_2_out;

  or or_1 (Out, not_1_out, and_1_out);
  not not_1 (not_1_out, S0_in);
  not not_2 (not_2_out, S9_in);
  and and_1 (and_1_out, not_2_out, ResetReg_in);
endmodule
