// Logisim project circuito_jump.circ as structural Verilog: 2 circuits, main circuit main
module main (
  input  ENDERECO,
  input  JUMP,
  input  CLEAR,
  output VAI_NO_SET,
  output VAI_NO_RESET
);

  wire not_1_out, or_1_out;

  not not_1 (not_1_out, JUMP);
  or or_1 (or_1_out, ENDERECO, not_1_out);
  and and_1 (VAI_NO_RESET, or_1_out, CLEAR);
  nand nand_1 (VAI_NO_SET, ENDERECO, JUMP);
endmodule

module jump_fechado (
  input  end0,
  input  jump0,
  input  clear0,
  input  end1,
  input  jump1,
  input  clear1,
  input  end2,
  input  jump2,
  input  clear2,
  input  end3,
  input  jump3,
  input  clear3,
  input  end4,
  input  jump4,
  input  clear4,
  input  end5,
  input  jump5,
  input  clear5,
  input  end6,
  input  jump6,
  input  clear6,
  input  end7,
  input  jump7,
  input  clear7,
  output set0,
  output reset0,
  output set1,
  output reset1,
  output set2,
  output reset2,
  output set3,
  output reset3,
  output set4,
  output reset4,
  output set5,
  output reset5,
  output set6,
  output reset6,
  output set7,
  output reset7
);

  main main_1 (.ENDERECO(end0), .JUMP(jump0), .CLEAR(clear0), .VAI_NO_SET(set0), .VAI_NO_RESET(reset0));
  main main_2 (.ENDERECO(end1), .JUMP(jump1), .CLEAR(clear1), .VAI_NO_SET(set1), .VAI_NO_RESET(reset1));
  main main_3 (.ENDERECO(end2), .JUMP(jump2), .CLEAR(clear2), .VAI_NO_SET(set2), .VAI_NO_RESET(reset2));
  main main_4 (.ENDERECO(end3), .JUMP(jump3), .CLEAR(clear3), .VAI_NO_SET(set3), .VAI_NO_RESET(reset3));
  main main_5 (.ENDERECO(end4), .JUMP(jump4), .CLEAR(clear4), .VAI_NO_SET(set4), .VAI_NO_RESET(reset4));
  main main_6 (.ENDERECO(end5), .JUMP(jump5), .CLEAR(clear5), .VAI_NO_SET(set5), .VAI_NO_RESET(reset5));
  main main_7 (.ENDERECO(end6), .JUMP(jump6), .CLEAR(clear6), .VAI_NO_SET(set6), .VAI_NO_RESET(reset6));
  main main_8 (.ENDERECO(end7), .JUMP(jump7), .CLEAR(clear7), .VAI_NO_SET(set7), .VAI_NO_RESET(reset7));
endmodule
